// Digital circuit EXP4.dig as structural Verilog
module EXP4 (
  output Q0,
  output Q1,
  output Q2,
  output Q3
);

  wire button_1_out;

  Button button_1 (.out(button_1_out));
  JK_FF jk_ff_1 (.J(1'b1), .C(button_1_out), .K(1'b1), .Q(Q0));  // open: nQ
  JK_FF jk_ff_2 (.J(1'b1), .C(Q0), .K(1'b1), .Q(Q1));  // open: nQ
  JK_FF jk_ff_3 (.J(1'b1), .C(Q1), .K(1'b1), .Q(Q2));  // open: nQ
  JK_FF jk_ff_4 (.J(1'b1), .C(Q2), .K(1'b1), .Q(Q3));  // open: nQ
endmodule
