// Digital circuit circuito_somador_4bits.dig as structural Verilog
module circuito_somador_4bits (
  input  A0,
  input  B0,
  input  Ci,
  input  A1,
  input  B1,
  input  A2,
  input  B2,
  input  A3,
  input  B3
);

  wire and_1_out, and_2_out, and_3_out, and_4_out, and_5_out, and_6_out, and_7_out, and_8_out, and_9_out,
       and_10_out, and_11_out, and_12_out, or_1_out, or_2_out, or_3_out, or_4_out, xor_1_out, xor_2_out,
       xor_3_out, xor_4_out, xor_5_out, xor_6_out, xor_7_out, xor_8_out;

  xor xor_1 (xor_1_out, A0, B0);
  and and_1 (and_1_out, Ci, B0);
  and and_2 (and_2_out, Ci, A0);
  and and_3 (and_3_out, B0, A0);
  xor xor_2 (xor_2_out, xor_1_out, Ci);
  or or_1 (or_1_out, and_1_out, and_2_out, and_3_out);
  LED S0 (.in(xor_2_out));
  xor xor_3 (xor_3_out, B1, A1);
  and and_4 (and_4_out, B1, A1);
  and and_5 (and_5_out, B1, or_1_out);
  and and_6 (and_6_out, A1, or_1_out);
  xor xor_4 (xor_4_out, xor_3_out, or_1_out);
  or or_2 (or_2_out, and_4_out, and_5_out, and_6_out);
  LED S1 (.in(xor_4_out));
  xor xor_5 (xor_5_out, B2, A2);
  and and_7 (and_7_out, B2, A2);
  and and_8 (and_8_out, B2, or_2_out);
  and and_9 (and_9_out, A2, or_2_out);
  xor xor_6 (xor_6_out, xor_5_out, or_2_out);
  or or_3 (or_3_out, and_7_out, and_8_out, and_9_out);
  LED S2 (.in(xor_6_out));
  xor xor_7 (xor_7_out, B3, A3);
  and and_10 (and_10_out, B3, A3);
  and and_11 (and_11_out, B3, or_3_out);
  and and_12 (and_12_out, A3, or_3_out);
  xor xor_8 (xor_8_out, xor_7_out, or_3_out);
  or or_4 (or_4_out, and_10_out, and_11_out, and_12_out);
  LED S3 (.in(xor_8_out));
  LED Co (.in(or_4_out));
endmodule

/* Test case:
Ci A0 A1 A2 A3 B0 B1 B2 B3 S0 S1 S2 S3 Co
0  0  0  0  0  0  0  0  0  0  0  0  0  0
0  1  0  0  0  1  0  0  0  0  1  0  0  0
0  0  1  1  0  1  1  0  0  1  0  0  1  0
0  1  1  1  1  0  1  0  0  1  0  0  0  1
0  1  1  1  0  0  0  0  1  1  1  1  1  0
0  0  0  0  1  0  0  0  1  0  0  0  0  1
0  0  1  0  1  1  1  0  0  1  0  1  1  0
0  0  1  0  1  0  1  0  1  0  0  1  0  1
*/
