// Digital circuit exp2.dig as structural Verilog
module exp2 (
  input  RESET,
  input  SET,
  input  in_7,
  input  in_8,
  input  in_11,
  input  in_12,
  input  in_15,
  input  in_16,
  input  in_19,
  input  in_20,
  input  R,
  input  S,
  input  in_25,
  input  RESET_2,
  input  SET_2,
  input  RESET_3,
  output Q,
  output Q_2,
  output out_5,
  output out_6,
  output out_9,
  output out_10,
  output out_13,
  output out_14,
  output out_17,
  output out_18,
  output Q_3,
  output Q_4,
  output Q_5,
  output Q_6
);

  wire and_1_out, and_2_out, and_3_out, and_4_out, and_5_out, and_6_out, not_1_out;

  // NOr nor_1 is placed but not wired
  // NOr nor_2 is placed but not wired
  nor nor_3 (out_5, in_7, out_6);
  nor nor_4 (out_6, out_5, in_8);
  nor nor_5 (out_9, in_11, out_10);
  nor nor_6 (out_10, out_9, in_12);
  nor nor_7 (out_13, in_15, out_14);
  nor nor_8 (out_14, out_13, in_16);
  nor nor_9 (out_17, in_19, out_18);
  nor nor_10 (out_18, out_17, in_20);
  nor nor_11 (Q_3, R, Q_4);
  nor nor_12 (Q_4, Q_3, S);
  // NOr nor_13 is placed but not wired
  Button clock ();  // open: out
  Button clock_2 ();  // open: out
  not not_1 (not_1_out, in_25);
  and and_1 (and_1_out, not_1_out, in_25);
  // And and_2 has open pins: In_1=open, In_2=open, out=and_2_out
  and and_3 (and_3_out, SET_2, and_1_out);
  and and_4 (and_4_out, and_1_out, RESET_2);
  and and_5 (and_5_out, SET, and_2_out);
  and and_6 (and_6_out, and_2_out, RESET);
  RS_FF_AS rs_ff_as_1 (.S(and_3_out), .R(and_4_out), .Q(Q_5), .nQ(Q_6));
  RS_FF_AS rs_ff_as_2 (.S(and_5_out), .R(and_6_out), .Q(Q), .nQ(Q_2));
endmodule
